// Logisim project logisimCircuit.circ as structural Verilog: 5 circuits, main circuit main
module main (
);

  wire and_1_out, clock_1_out, clock_2_out, clock_3_out, controler_1_jmp, controler_1_memwr,
       controler_1_regwr, isnotzero_1_res, not_1_out;
  wire [1:0] controler_1_alu___reg___imm___mem;
  wire [2:0] controler_1_operand, controler_1_r0c, controler_1_r1c;
  wire [7:0] adder_1_out, controler_1_imm8, multiplexer_1_out, register_1_q;
  wire [15:0] alu_1_out_4, multiplexer_2_out, ram_1_data, regfile_1_r0d, regfile_1_r1d, rom_1_data;

  isNotZero isnotzero_1 (.\input (regfile_1_r0d), .res(isnotzero_1_res));
  Adder adder_1 (.a(register_1_q), .b(8'h1), .out(adder_1_out));  // open: cin, cout
  Multiplexer #(.width(8), .disabled(0), .enable("false")) multiplexer_1 (
    .in0(adder_1_out), .in1(controler_1_imm8), .out(multiplexer_1_out), .sel(and_1_out));
  Clock clock_1 (.out(clock_1_out));
  and and_1 (and_1_out, isnotzero_1_res, controler_1_jmp);
  Register register_1 (.D(multiplexer_1_out), .Q(register_1_q), .clk(clock_1_out));  // open: en, clr
  ROM #(.dataWidth(16)) rom_1 (.addr(register_1_q), .data(rom_1_data));  // open: sel
  Controler controler_1 (
    .INSTRUCTION(rom_1_data), .jmp(controler_1_jmp), .regWr(controler_1_regwr), .R0c(controler_1_r0c),
    .R1c(controler_1_r1c), .Imm8(controler_1_imm8), .Operand(controler_1_operand), .memWr(controler_1_memwr),
    .alu___reg___imm___mem(controler_1_alu___reg___imm___mem));
  Clock clock_2 (.out(clock_2_out));
  RegFile regfile_1 (
    .R0d(regfile_1_r0d), .R1d(regfile_1_r1d), .CLK(clock_2_out), .data(multiplexer_2_out),
    .wrEn(controler_1_regwr), .R0c(controler_1_r0c), .R1c(controler_1_r1c));
  ALU alu_1 (.IN0(regfile_1_r0d), .IN1(regfile_1_r1d), .OPERAND(controler_1_operand), .out_4(alu_1_out_4));
  Multiplexer #(.select(2), .width(16), .disabled(0), .enable("false")) multiplexer_2 (
    .in0(ram_1_data), .in1({{8{1'b0}}, controler_1_imm8}), .in2(regfile_1_r1d), .in3(alu_1_out_4),
    .out(multiplexer_2_out), .sel(controler_1_alu___reg___imm___mem));
  RAM #(.addrWidth(16), .dataWidth(16), .bus("separate")) ram_1 (
    .addr(regfile_1_r1d), .din(regfile_1_r0d), .data(ram_1_data), .str(controler_1_memwr), .clk(clock_3_out),
    .ld(not_1_out));  // open: sel, clr
  not not_1 (not_1_out, controler_1_memwr);
  Clock clock_3 (.out(clock_3_out));

  // Notes on the sheet:
  //   contents of rom_1 (hex, n*v repeats v):
  //   1200 1402 1a0a 1c02 640 4680 280 4c0 3600 5b80 ca08
endmodule

module ALU (
  input  [15:0] IN0,
  input  [15:0] IN1,
  input  [2:0] OPERAND,
  output [15:0] out_4
);

  wire [15:0] adder_1_out, and_1_out, not_1_out, or_1_out, shifter_1_out, shifter_2_out, subtractor_1_out,
       xor_1_out;

  Adder #(.width(16)) adder_1 (.a(IN0), .b(IN1), .out(adder_1_out));  // open: cin, cout
  Subtractor #(.width(16)) subtractor_1 (.a(IN0), .b(IN1), .out(subtractor_1_out));  // open: bin, bout
  assign and_1_out = IN0 & IN1;  // AND_Gate and_1, 16 bits wide
  assign or_1_out = IN0 | IN1;  // OR_Gate or_1, 16 bits wide
  assign xor_1_out = IN0 ^ IN1;  // XOR_Gate xor_1, 16 bits wide
  assign not_1_out = ~IN1;  // NOT_Gate not_1, 16 bits wide
  Shifter #(.width(16)) shifter_1 (.in(IN0), .\dist (IN1[3:0]), .out(shifter_1_out));
  Shifter #(.width(16), .shift("lr")) shifter_2 (.in(IN0), .\dist (IN1[3:0]), .out(shifter_2_out));
  Multiplexer #(.select(3), .width(16), .disabled(0), .enable("false")) multiplexer_1 (
    .in0(adder_1_out), .in1(subtractor_1_out), .in2(and_1_out), .in3(or_1_out), .in4(xor_1_out),
    .in5(not_1_out), .in6(shifter_1_out), .in7(shifter_2_out), .out(out_4), .sel(OPERAND));
endmodule

module RegFile (
  input  wrEn,
  input  [2:0] R0c,
  input  [2:0] R1c,
  input  CLK,
  input  [15:0] data,
  output [15:0] R0d,
  output [15:0] R1d
);

  wire demultiplexer_1_out1, demultiplexer_1_out2, demultiplexer_1_out3, demultiplexer_1_out4,
       demultiplexer_1_out5, demultiplexer_1_out6, demultiplexer_1_out7;
  wire [15:0] A_q, B_q, C_q, D_q, E_q, F_q, SP_q, ZERO_q;

  Demultiplexer #(.select(3), .disabled(0), .enable("false")) demultiplexer_1 (
    .out1(demultiplexer_1_out1), .out2(demultiplexer_1_out2), .out3(demultiplexer_1_out3),
    .out4(demultiplexer_1_out4), .out5(demultiplexer_1_out5), .out6(demultiplexer_1_out6),
    .out7(demultiplexer_1_out7), .in(wrEn), .sel(R0c));  // open: out0
  Register #(.width(16)) ZERO (.Q(ZERO_q));  // open: D, en, clk, clr
  Register #(.width(16)) A (.D(data), .en(demultiplexer_1_out1), .Q(A_q), .clk(CLK));  // open: clr
  Register #(.width(16)) B (.D(data), .en(demultiplexer_1_out2), .Q(B_q), .clk(CLK));  // open: clr
  Register #(.width(16)) C (.D(data), .en(demultiplexer_1_out3), .Q(C_q), .clk(CLK));  // open: clr
  Register #(.width(16)) D (.D(data), .en(demultiplexer_1_out4), .Q(D_q), .clk(CLK));  // open: clr
  Register #(.width(16)) E (.D(data), .en(demultiplexer_1_out5), .Q(E_q), .clk(CLK));  // open: clr
  Register #(.width(16)) F (.D(data), .en(demultiplexer_1_out6), .Q(F_q), .clk(CLK));  // open: clr
  Register #(.width(16)) SP (.D(data), .en(demultiplexer_1_out7), .Q(SP_q), .clk(CLK));  // open: clr
  Multiplexer #(.select(3), .width(16), .disabled(0), .enable("false")) multiplexer_1 (
    .in0(ZERO_q), .in1(A_q), .in2(B_q), .in3(C_q), .in4(D_q), .in5(E_q), .in6(F_q), .in7(SP_q), .out(R0d),
    .sel(R0c));
  Multiplexer #(.select(3), .width(16), .disabled(0), .enable("false")) multiplexer_2 (
    .in0(ZERO_q), .in1(A_q), .in2(B_q), .in3(C_q), .in4(D_q), .in5(E_q), .in6(F_q), .in7(SP_q), .out(R1d),
    .sel(R1c));
endmodule

module Controler (
  input  [15:0] INSTRUCTION,
  output jmp,
  output regWr,
  output [2:0] R0c,
  output [2:0] R1c,
  output [7:0] Imm8,
  output [2:0] Operand,
  output memWr,
  output [1:0] alu___reg___imm___mem
);

  Multiplexer #(.select(4), .width(8), .disabled(0), .enable("false")) multiplexer_1 (
    .in0(8'h42), .in1(8'h41), .in2(8'h40), .in3(8'h4), .in4(8'h43), .in5(8'h4b), .in6(8'h53), .in7(8'h5b),
    .in8(8'h63), .in9(8'h6b), .in10(8'h73), .in11(8'h7b), .in12(8'h80),
    .out({jmp, regWr, Operand, memWr, alu___reg___imm___mem}), .sel(INSTRUCTION[15:12]));  // open: in13, in14, in15

  assign Imm8 = INSTRUCTION[8:1];
  assign R0c = INSTRUCTION[11:9];
  assign R1c = INSTRUCTION[8:6];
endmodule

module isNotZero (
  input  [15:0] \input ,
  output res
);

  or or_1 (res, \input [0], \input [1], \input [2], \input [3], \input [4], \input [5], \input [6], \input [7], \input [8], \input [9], \input [10], \input [11], \input [12], \input [13], \input [14], \input [15]);
endmodule
